# Fritzing sketch OWIRobotArm (saved by Fritzing 0.9.1b)
breadboards: 1

parts:
  Part1 = Arduino Uno (Rev3)
  U4 = DRV8833
  U5 = DRV8833
  U6 = DRV8833
  M1 = DC Motor
  M2 = DC Motor
  M3 = DC Motor
  M4 = DC Motor
  M5 = DC Motor
  R1 = TRIMPOT [package=trimpot_pth_s3_lock]
  R2 = TRIMPOT [package=trimpot_pth_s3_lock]
  R3 = TRIMPOT [package=trimpot_pth_s3_lock]
  R4 = TRIMPOT [package=trimpot_pth_s3_lock]
  R5 = TRIMPOT [package=trimpot_pth_s3_lock]
  J1 = Screw terminal - 2 pins [package=THT]

nets:
  N1: Part1.A0, R1.WIPER
  N2: Part1.A1, R2.WIPER
  N3: Part1.A2, R3.WIPER
  N4: Part1.A3, R4.WIPER
  N5: Part1.A4/SDA, R5.WIPER
  N6: Part1.D8, U5.BIN1
  N7: Part1.D9_PWM, U6.AIN1
  N8: Part1.D10_PWM/SS, U6.AIN2
  N9: Part1.D11_PWM/MOSI, U6.BIN2
  N10: Part1.D12/MISO, U6.BIN1
  N11: Part1.D3_PWM, U4.BIN2
  N12: Part1.D4, U4.BIN1
  N13: Part1.D5_PWM, U5.AIN1
  N14: Part1.D6_PWM, U5.AIN2
  N15: Part1.D7, U5.BIN2
  N16: Part1.5V, R5.CW
  GND: Part1.GND, U4.GND, U5.GND, U6.GND, R5.CCW, J1.pin1
  VIN: U4.VIN, U5.VIN, U6.VIN, J1.pin2
  N17: U4.BOUT1, M5.pin_1
  N18: U4.BOUT2, M5.pin_2
  N19: U5.BOUT1, M3.pin_1
  N20: U5.BOUT2, M3.pin_2
  N21: U5.AOUT2, M4.pin_2
  N22: U5.AOUT1, M4.pin_1
  N23: U6.BOUT1, M1.pin_1
  N24: U6.BOUT2, M1.pin_2
  N25: U6.AOUT2, M2.pin_2
  N26: U6.AOUT1, M2.pin_1

custom parts:
  DRV8833: The DRV8833 provides a dual bridge motor driver solution for toys, printers, and other mechatronic applications.
